// Digital circuit mod_adder_plus_K.dig as structural Verilog
module mod_adder_plus_K (
  input  A0,
  input  A1,
  input  A2,
  input  A3,
  input  A4,
  input  A5,
  input  B0,
  input  B1,
  input  B2,
  input  B3,
  input  B4,
  input  B5,
  input  K0,
  input  K1,
  input  K2,
  input  K3,
  input  K4,
  input  K5,
  input  _0_3,
  input  _0_1,
  input  _0_2,
  input  _0_8,
  input  _0_5,
  input  _0_6,
  input  _0_7,
  input  _0_4,
  output s6,
  output s5,
  output s4,
  output s3,
  output s2,
  output s1,
  output s0
);

  wire add_1_s, add_2_c_o, add_2_s, add_3_c_o, add_3_s, add_4_c_o, add_4_s, add_5_c_o, add_5_s, add_6_c_o,
       add_6_s, and_1_out, and_2_out, and_3_out, and_4_out, and_5_out, and_6_out, and_7_out, and_8_out,
       and_9_out, and_10_out, and_11_out, and_12_out, and_13_out, and_14_out, and_15_out, and_16_out,
       and_17_out, and_18_out, and_19_out, and_20_out, and_21_out, and_22_out, and_23_out, and_24_out,
       and_25_out, and_26_out, and_27_out, and_28_out, and_29_out, and_30_out, and_31_out, and_32_out,
       and_33_out, and_34_out, and_35_out, and_36_out, and_37_out, and_38_out, and_39_out, and_40_out,
       and_41_out, and_42_out, and_43_out, and_44_out, and_45_out, multiplexer_1_out, multiplexer_2_out,
       multiplexer_3_out, multiplexer_4_out, multiplexer_5_out, multiplexer_6_out, multiplexer_7_out,
       multiplexer_8_out, multiplexer_9_out, multiplexer_10_out, multiplexer_11_out, multiplexer_12_out,
       multiplexer_13_out, multiplexer_14_out, multiplexer_15_out, multiplexer_16_out, multiplexer_17_out,
       multiplexer_18_out, multiplexer_19_out, multiplexer_20_out, multiplexer_21_out, multiplexer_22_out,
       multiplexer_23_out, multiplexer_24_out, multiplexer_25_out, multiplexer_26_out, not_1_out, not_2_out,
       not_3_out, not_4_out, not_5_out, not_6_out, not_7_out, not_8_out, not_9_out, not_10_out, not_11_out,
       not_12_out, not_13_out, not_14_out, or_1_out, or_2_out, or_3_out, or_4_out, or_5_out, or_6_out,
       or_7_out, or_8_out, or_9_out, or_10_out, or_11_out, or_12_out, or_13_out, or_14_out, or_15_out,
       or_16_out, or_17_out, or_18_out, or_19_out, or_20_out, or_21_out, or_22_out, or_23_out, or_24_out,
       or_25_out, or_26_out, or_27_out, or_28_out, or_29_out, or_30_out, or_31_out, or_32_out, xor_8_out,
       xor_9_out, xor_10_out, xor_11_out, xor_12_out, xor_13_out, xor_14_out;

  or or_1 (or_1_out, or_5_out, or_4_out);
  not not_1 (not_1_out, or_1_out);
  and and_1 (and_1_out, _0_7, _0_6);
  and and_2 (and_2_out, or_6_out, ~and_1_out);  // And
  and and_3 (and_3_out, multiplexer_10_out, multiplexer_8_out);
  and and_4 (and_4_out, or_6_out, or_8_out);
  or or_2 (or_2_out, and_4_out, and_1_out);
  and and_5 (and_5_out, or_7_out, or_9_out);
  or or_3 (or_3_out, and_5_out, and_3_out);
  and and_6 (and_6_out, and_8_out, or_21_out);
  or or_4 (or_4_out, and_6_out, or_2_out);
  and and_7 (and_7_out, and_9_out, or_18_out);
  or or_5 (or_5_out, and_7_out, or_3_out);
  or or_6 (or_6_out, _0_7, _0_6);
  or or_7 (or_7_out, multiplexer_10_out, multiplexer_8_out);
  and and_8 (and_8_out, or_13_out, or_6_out);
  and and_9 (and_9_out, and_18_out, or_7_out);
  or or_8 (or_8_out, and_13_out, and_10_out);
  or or_9 (or_9_out, and_14_out, and_12_out);
  Multiplexer multiplexer_1 (.sel(not_1_out), .in_0(or_11_out), .in_1(or_10_out), .out(multiplexer_1_out));
  and and_10 (and_10_out, B5, A5);
  and and_11 (and_11_out, or_12_out, ~and_10_out);  // And
  and and_12 (and_12_out, multiplexer_12_out, multiplexer_9_out);
  and and_13 (and_13_out, or_12_out, and_19_out);
  and and_14 (and_14_out, or_13_out, and_20_out);
  and and_15 (and_15_out, and_17_out, or_21_out);
  or or_10 (or_10_out, and_15_out, or_8_out);
  and and_16 (and_16_out, and_18_out, or_18_out);
  or or_11 (or_11_out, and_16_out, or_9_out);
  or or_12 (or_12_out, B5, A5);
  or or_13 (or_13_out, multiplexer_12_out, multiplexer_9_out);
  and and_17 (and_17_out, or_16_out, or_12_out);
  and and_18 (and_18_out, or_17_out, or_13_out);
  and and_19 (and_19_out, B4, A4);
  and and_20 (and_20_out, multiplexer_14_out, multiplexer_11_out);
  and and_21 (and_21_out, or_16_out, or_21_out);
  or or_14 (or_14_out, and_21_out, and_19_out);
  and and_22 (and_22_out, or_17_out, or_18_out);
  or or_15 (or_15_out, and_22_out, and_20_out);
  Multiplexer multiplexer_2 (.sel(not_1_out), .in_0(or_15_out), .in_1(or_14_out), .out(multiplexer_2_out));
  or or_16 (or_16_out, B4, A4);
  and and_23 (and_23_out, or_16_out, ~and_19_out);  // And
  or or_17 (or_17_out, multiplexer_14_out, multiplexer_11_out);
  or or_18 (or_18_out, and_29_out, or_20_out);
  Multiplexer multiplexer_3 (.sel(not_1_out), .in_0(or_18_out), .in_1(or_21_out), .out(multiplexer_3_out));
  and and_24 (and_24_out, B3, A3);
  and and_25 (and_25_out, multiplexer_16_out, multiplexer_13_out);
  and and_26 (and_26_out, or_22_out, and_33_out);
  or or_19 (or_19_out, and_26_out, and_24_out);
  and and_27 (and_27_out, or_23_out, and_34_out);
  or or_20 (or_20_out, and_27_out, and_25_out);
  and and_28 (and_28_out, and_31_out, or_29_out);
  or or_21 (or_21_out, and_28_out, or_19_out);
  and and_29 (and_29_out, and_32_out, or_28_out);
  or or_22 (or_22_out, B3, A3);
  and and_30 (and_30_out, or_22_out, ~and_24_out);  // And
  or or_23 (or_23_out, multiplexer_16_out, multiplexer_13_out);
  and and_31 (and_31_out, or_26_out, or_22_out);
  and and_32 (and_32_out, or_27_out, or_23_out);
  and and_33 (and_33_out, B2, A2);
  and and_34 (and_34_out, multiplexer_18_out, multiplexer_15_out);
  and and_35 (and_35_out, or_26_out, or_29_out);
  or or_24 (or_24_out, and_35_out, and_33_out);
  and and_36 (and_36_out, or_27_out, or_28_out);
  or or_25 (or_25_out, and_36_out, and_34_out);
  Multiplexer multiplexer_4 (.sel(not_1_out), .in_0(or_25_out), .in_1(or_24_out), .out(multiplexer_4_out));
  or or_26 (or_26_out, B2, A2);
  and and_37 (and_37_out, or_26_out, ~and_33_out);  // And
  or or_27 (or_27_out, multiplexer_18_out, multiplexer_15_out);
  or or_28 (or_28_out, and_42_out, and_40_out);
  and and_38 (and_38_out, B1, A1);
  and and_39 (and_39_out, or_30_out, ~and_38_out);  // And
  and and_40 (and_40_out, multiplexer_20_out, multiplexer_17_out);
  and and_41 (and_41_out, or_30_out, and_43_out);
  or or_29 (or_29_out, and_41_out, and_38_out);
  and and_42 (and_42_out, or_31_out, and_44_out);
  Multiplexer multiplexer_5 (.sel(not_1_out), .in_0(or_28_out), .in_1(or_29_out), .out(multiplexer_5_out));
  or or_30 (or_30_out, B1, A1);
  or or_31 (or_31_out, multiplexer_20_out, multiplexer_17_out);
  and and_43 (and_43_out, B0, A0);
  and and_44 (and_44_out, _0_3, multiplexer_19_out);
  Multiplexer multiplexer_6 (.sel(not_1_out), .in_0(and_44_out), .in_1(and_43_out), .out(multiplexer_6_out));
  or or_32 (or_32_out, B0, A0);
  and and_45 (and_45_out, or_32_out, ~and_43_out);  // And
  // Or or_33 has open pins: In_1=_0_3, In_2=multiplexer_19_out, out=open
  Multiplexer multiplexer_7 (.sel(not_1_out), .in_0(xor_14_out), .in_1(and_45_out), .out(multiplexer_7_out));
  xor xor_1 (s6, multiplexer_21_out, multiplexer_1_out);
  xor xor_2 (s5, multiplexer_22_out, multiplexer_2_out);
  not not_2 (not_2_out, and_2_out);
  xor xor_3 (s4, multiplexer_23_out, multiplexer_3_out);
  not not_3 (not_3_out, K5);
  Add add_1 (.a(not_3_out), .b(_0_5), .c_i(add_2_c_o), .s(add_1_s));  // open: c_o
  not not_4 (not_4_out, and_11_out);
  Multiplexer multiplexer_8 (.sel(_0_4), .in_0(and_2_out), .in_1(not_2_out), .out(multiplexer_8_out));
  not not_5 (not_5_out, K4);
  Add add_2 (.a(not_5_out), .b(_0_5), .c_i(add_3_c_o), .s(add_2_s), .c_o(add_2_c_o));
  not not_6 (not_6_out, and_23_out);
  Multiplexer multiplexer_9 (.sel(add_1_s), .in_0(and_11_out), .in_1(not_4_out), .out(multiplexer_9_out));
  Multiplexer multiplexer_10 (.sel(add_1_s), .in_0(and_10_out), .in_1(or_12_out), .out(multiplexer_10_out));
  xor xor_4 (s3, multiplexer_24_out, multiplexer_4_out);
  not not_7 (not_7_out, and_30_out);
  Multiplexer multiplexer_11 (.sel(add_2_s), .in_0(and_23_out), .in_1(not_6_out), .out(multiplexer_11_out));
  Multiplexer multiplexer_12 (.sel(add_2_s), .in_0(and_19_out), .in_1(or_16_out), .out(multiplexer_12_out));
  xor xor_5 (s2, multiplexer_25_out, multiplexer_5_out);
  not not_8 (not_8_out, K3);
  Add add_3 (.a(not_8_out), .b(_0_5), .c_i(add_4_c_o), .s(add_3_s), .c_o(add_3_c_o));
  not not_9 (not_9_out, and_37_out);
  Multiplexer multiplexer_13 (.sel(add_3_s), .in_0(and_30_out), .in_1(not_7_out), .out(multiplexer_13_out));
  Multiplexer multiplexer_14 (.sel(add_3_s), .in_0(and_24_out), .in_1(or_22_out), .out(multiplexer_14_out));
  xor xor_6 (s1, multiplexer_26_out, multiplexer_6_out);
  not not_10 (not_10_out, K2);
  Add add_4 (.a(not_10_out), .b(_0_5), .c_i(add_5_c_o), .s(add_4_s), .c_o(add_4_c_o));
  not not_11 (not_11_out, and_39_out);
  Multiplexer multiplexer_15 (.sel(add_4_s), .in_0(and_37_out), .in_1(not_9_out), .out(multiplexer_15_out));
  Multiplexer multiplexer_16 (.sel(add_4_s), .in_0(and_33_out), .in_1(or_26_out), .out(multiplexer_16_out));
  xor xor_7 (s0, _0_2, multiplexer_7_out);
  not not_12 (not_12_out, K1);
  Add add_5 (.a(not_12_out), .b(_0_5), .c_i(add_6_c_o), .s(add_5_s), .c_o(add_5_c_o));
  not not_13 (not_13_out, and_45_out);
  Multiplexer multiplexer_17 (.sel(add_5_s), .in_0(and_39_out), .in_1(not_11_out), .out(multiplexer_17_out));
  Multiplexer multiplexer_18 (.sel(add_5_s), .in_0(and_38_out), .in_1(or_30_out), .out(multiplexer_18_out));
  not not_14 (not_14_out, K0);
  Add add_6 (.a(not_14_out), .b(_0_8), .c_i(_0_5), .s(add_6_s), .c_o(add_6_c_o));
  Multiplexer multiplexer_19 (.sel(add_6_s), .in_0(and_45_out), .in_1(not_13_out), .out(multiplexer_19_out));
  Multiplexer multiplexer_20 (.sel(add_6_s), .in_0(and_43_out), .in_1(or_32_out), .out(multiplexer_20_out));
  Multiplexer multiplexer_21 (.sel(not_1_out), .in_0(xor_8_out), .in_1(and_2_out), .out(multiplexer_21_out));
  xor xor_8 (xor_8_out, multiplexer_8_out, multiplexer_10_out);
  Multiplexer multiplexer_22 (.sel(not_1_out), .in_0(xor_9_out), .in_1(and_11_out), .out(multiplexer_22_out));
  xor xor_9 (xor_9_out, multiplexer_9_out, multiplexer_12_out);
  Multiplexer multiplexer_23 (.sel(not_1_out), .in_0(xor_10_out), .in_1(and_23_out), .out(multiplexer_23_out));
  xor xor_10 (xor_10_out, multiplexer_11_out, multiplexer_14_out);
  Multiplexer multiplexer_24 (.sel(not_1_out), .in_0(xor_11_out), .in_1(and_30_out), .out(multiplexer_24_out));
  xor xor_11 (xor_11_out, multiplexer_13_out, multiplexer_16_out);
  Multiplexer multiplexer_25 (.sel(not_1_out), .in_0(xor_12_out), .in_1(and_37_out), .out(multiplexer_25_out));
  xor xor_12 (xor_12_out, multiplexer_15_out, multiplexer_18_out);
  Multiplexer multiplexer_26 (.sel(not_1_out), .in_0(xor_13_out), .in_1(and_39_out), .out(multiplexer_26_out));
  xor xor_13 (xor_13_out, multiplexer_17_out, multiplexer_20_out);
  xor xor_14 (xor_14_out, multiplexer_19_out, _0_1);

  // Notes on the sheet:
  //   _0_8: default 1
endmodule
